// Logisim project Quartz_version_0.circ as structural Verilog: 1 circuit, main circuit main
module main (
);

  wire adder_1_cout, and_1_out, and_2_out, C_ALU_ADD_ENABLE, C_ALU_DATA_ENABLE, C_ALU_IDX_SEL, C_CIR_LATCH,
       C_CLOCK, C_IDX_ENABLE, C_IDX_LATCH, C_MAR_LATCH, C_MDR_ENABLE, C_MDR_LATCH, C_MEM_READ, C_MEM_WRITE,
       C_PC_ENABLE, C_PC_LATCH, C_RA_ENABLE, C_RA_LATCH, C_RB_ENABLE, C_RB_LATCH, C_RESET, C_TX_H, C_TX_L,
       d_ff_1_q, F_CIN, multiplexer_11_out, not_1_out, not_2_out, or_1_out, or_2_out, or_3_out, or_4_out,
       por_1_out, RESET_out, undriven, undriven_2, undriven_3, undriven_4;
  wire [1:0] C_ALU_SFT_OP, multiplexer_1_out, multiplexer_1_out_2, multiplexer_1_out_3, multiplexer_1_out_4,
       multiplexer_1_out_5, multiplexer_1_out_6, multiplexer_1_out_7, multiplexer_1_out_8;
  wire [3:0] adder_2_out, C_ALU_BW_OP, MIC_q;
  wire [7:0] adder_1_out, CIR_q, controlled_buffer_1_out, controlled_buffer_1_out_2, controlled_buffer_4_out,
       controlled_buffer_6_out, controlled_buffer_9_out, MDR_q, multiplexer_2_out, multiplexer_10_out,
       multiplexer_12_out, RA_q, ram_1_dout, rom_1_data;
  wire [15:0] IDX_q, MAR_q, PC_q;
  wire [15:11] CBUS_2;

  Register #(.width(16)) PC (
    .D({controlled_buffer_1_out_2, controlled_buffer_1_out}), .en(C_PC_LATCH), .clk(C_CLOCK), .Q(PC_q),
    .clr(C_RESET));
  assign {controlled_buffer_1_out_2, controlled_buffer_1_out} = C_PC_ENABLE ? PC_q : 16'bz;  // Controlled_Buffer controlled_buffer_1
  Pull_Resistor pull_resistor_1 (.node(F_CIN));
  Pull_Resistor pull_resistor_2 (.node({controlled_buffer_1_out_2, controlled_buffer_1_out}));
  // Probe on {controlled_buffer_1_out_2, controlled_buffer_1_out}
  Pull_Resistor pull_resistor_3 (.node(controlled_buffer_1_out_2));
  Register #(.width(16)) MAR (
    .D({controlled_buffer_1_out_2, controlled_buffer_1_out}), .en(C_MAR_LATCH), .clk(C_CLOCK), .Q(MAR_q),
    .clr(C_RESET));
  Register #(.width(16)) IDX (
    .D({controlled_buffer_1_out_2, controlled_buffer_1_out}), .en(C_IDX_LATCH), .clk(C_CLOCK), .Q(IDX_q),
    .clr(C_RESET));
  ROM #(.addrWidth(15)) rom_1 (.addr(MAR_q[14:0]), .data(rom_1_data));
  RAM #(.addrWidth(15)) ram_1 (
    .addr(MAR_q[14:0]), .we(C_MEM_WRITE), .oe(not_1_out), .clk(C_CLOCK), .din(controlled_buffer_6_out),
    .dout(ram_1_dout));
  not not_1 (not_1_out, C_MEM_WRITE);
  assign controlled_buffer_1_out = C_IDX_ENABLE ? IDX_q[7:0] : 8'bz;  // Controlled_Buffer controlled_buffer_2
  assign controlled_buffer_1_out_2 = or_1_out ? IDX_q[15:8] : 8'bz;  // Controlled_Buffer controlled_buffer_3
  or or_1 (or_1_out, C_ALU_DATA_ENABLE, C_IDX_ENABLE);
  not not_2 (not_2_out, MAR_q[15]);
  and and_1 (and_1_out, C_MEM_READ, not_2_out);
  and and_2 (and_2_out, MAR_q[15], C_MEM_READ);
  assign controlled_buffer_4_out = and_1_out ? rom_1_data : 8'bz;  // Controlled_Buffer controlled_buffer_4
  assign controlled_buffer_4_out = and_2_out ? ram_1_dout : 8'bz;  // Controlled_Buffer controlled_buffer_5
  Multiplexer #(.width(8)) multiplexer_1 (
    .in0(RA_q), .in1(controlled_buffer_1_out),
    .out({multiplexer_1_out_8[0], multiplexer_1_out_7[0], multiplexer_1_out_6[0], multiplexer_1_out_5[0], multiplexer_1_out_4[0], multiplexer_1_out_3[0], multiplexer_1_out_2[0], multiplexer_1_out[0]}),
    .sel(C_ALU_IDX_SEL));
  Multiplexer #(.select(2)) multiplexer_2 (
    .in0(C_ALU_BW_OP[0]), .in1(C_ALU_BW_OP[1]), .in2(C_ALU_BW_OP[2]), .in3(C_ALU_BW_OP[3]),
    .out(multiplexer_2_out[0]), .sel(multiplexer_1_out));
  Multiplexer #(.select(2)) multiplexer_3 (
    .in0(C_ALU_BW_OP[0]), .in1(C_ALU_BW_OP[1]), .in2(C_ALU_BW_OP[2]), .in3(C_ALU_BW_OP[3]),
    .out(multiplexer_2_out[1]), .sel(multiplexer_1_out_2));
  Multiplexer #(.select(2)) multiplexer_4 (
    .in0(C_ALU_BW_OP[0]), .in1(C_ALU_BW_OP[1]), .in2(C_ALU_BW_OP[2]), .in3(C_ALU_BW_OP[3]),
    .out(multiplexer_2_out[2]), .sel(multiplexer_1_out_3));
  Multiplexer #(.select(2)) multiplexer_5 (
    .in0(C_ALU_BW_OP[0]), .in1(C_ALU_BW_OP[1]), .in2(C_ALU_BW_OP[2]), .in3(C_ALU_BW_OP[3]),
    .out(multiplexer_2_out[3]), .sel(multiplexer_1_out_4));
  Multiplexer #(.select(2)) multiplexer_6 (
    .in0(C_ALU_BW_OP[0]), .in1(C_ALU_BW_OP[1]), .in2(C_ALU_BW_OP[2]), .in3(C_ALU_BW_OP[3]),
    .out(multiplexer_2_out[4]), .sel(multiplexer_1_out_5));
  Multiplexer #(.select(2)) multiplexer_7 (
    .in0(C_ALU_BW_OP[0]), .in1(C_ALU_BW_OP[1]), .in2(C_ALU_BW_OP[2]), .in3(C_ALU_BW_OP[3]),
    .out(multiplexer_2_out[5]), .sel(multiplexer_1_out_6));
  Multiplexer #(.select(2)) multiplexer_8 (
    .in0(C_ALU_BW_OP[0]), .in1(C_ALU_BW_OP[1]), .in2(C_ALU_BW_OP[2]), .in3(C_ALU_BW_OP[3]),
    .out(multiplexer_2_out[6]), .sel(multiplexer_1_out_7));
  Multiplexer #(.select(2)) multiplexer_9 (
    .in0(C_ALU_BW_OP[0]), .in1(C_ALU_BW_OP[1]), .in2(C_ALU_BW_OP[2]), .in3(C_ALU_BW_OP[3]),
    .out(multiplexer_2_out[7]), .sel(multiplexer_1_out_8));
  Multiplexer #(.select(2), .width(8)) multiplexer_10 (
    .in0({multiplexer_1_out_8[0], multiplexer_1_out_7[0], multiplexer_1_out_6[0], multiplexer_1_out_5[0], multiplexer_1_out_4[0], multiplexer_1_out_3[0], multiplexer_1_out_2[0], multiplexer_1_out[0]}),
    .in1({multiplexer_1_out_7[0], multiplexer_1_out_6[0], multiplexer_1_out_5[0], multiplexer_1_out_4[0], multiplexer_1_out_3[0], multiplexer_1_out_2[0], multiplexer_1_out[0], F_CIN}),
    .in2({F_CIN, multiplexer_1_out_8[0], multiplexer_1_out_7[0], multiplexer_1_out_6[0], multiplexer_1_out_5[0], multiplexer_1_out_4[0], multiplexer_1_out_3[0], multiplexer_1_out_2[0]}),
    .in3({8{1'b0}}), .out(multiplexer_10_out), .sel(C_ALU_SFT_OP));
  Multiplexer #(.select(2)) multiplexer_11 (
    .in0(F_CIN), .in1(multiplexer_1_out[0]), .in2(multiplexer_1_out_8[0]), .in3(1'b0),
    .out(multiplexer_11_out), .sel(C_ALU_SFT_OP));
  assign controlled_buffer_6_out = C_MEM_WRITE ? MDR_q : 8'bz;  // Controlled_Buffer controlled_buffer_6
  Adder adder_1 (.a(multiplexer_10_out), .b(multiplexer_2_out), .out(adder_1_out), .cin(F_CIN), .cout(adder_1_cout));
  assign controlled_buffer_4_out = C_MDR_LATCH ? controlled_buffer_9_out : 8'bz;  // Controlled_Buffer controlled_buffer_7
  or or_2 (or_2_out, C_MDR_LATCH, C_MEM_READ);
  Register MDR (.D(controlled_buffer_4_out), .en(or_2_out), .clk(C_CLOCK), .Q(MDR_q), .clr(C_RESET));
  Register RA (.D(controlled_buffer_9_out), .en(C_RA_LATCH), .clk(C_CLOCK), .Q(RA_q), .clr(C_RESET));
  Register RB (
    .D(controlled_buffer_9_out), .en(C_RB_LATCH), .clk(C_CLOCK),
    .Q({multiplexer_1_out_8[1], multiplexer_1_out_7[1], multiplexer_1_out_6[1], multiplexer_1_out_5[1], multiplexer_1_out_4[1], multiplexer_1_out_3[1], multiplexer_1_out_2[1], multiplexer_1_out[1]}),
    .clr(C_RESET));
  assign controlled_buffer_1_out = C_ALU_ADD_ENABLE ? adder_1_out : 8'bz;  // Controlled_Buffer controlled_buffer_8
  assign controlled_buffer_9_out = C_MDR_ENABLE ? MDR_q : 8'bz;  // Controlled_Buffer controlled_buffer_9
  assign controlled_buffer_9_out = C_RA_ENABLE ? RA_q : 8'bz;  // Controlled_Buffer controlled_buffer_10
  assign controlled_buffer_9_out = C_RB_ENABLE ? {multiplexer_1_out_8[1], multiplexer_1_out_7[1], multiplexer_1_out_6[1], multiplexer_1_out_5[1], multiplexer_1_out_4[1], multiplexer_1_out_3[1], multiplexer_1_out_2[1], multiplexer_1_out[1]} : 8'bz;  // Controlled_Buffer controlled_buffer_11
  assign controlled_buffer_9_out = C_ALU_DATA_ENABLE ? adder_1_out : 8'bz;  // Controlled_Buffer controlled_buffer_12
  assign controlled_buffer_1_out_2 = C_TX_H ? controlled_buffer_9_out : 8'bz;  // Controlled_Buffer controlled_buffer_13
  Pull_Resistor pull_resistor_4 (.node(controlled_buffer_9_out));
  // Probe on controlled_buffer_9_out
  assign controlled_buffer_1_out = C_TX_L ? controlled_buffer_9_out : 8'bz;  // Controlled_Buffer controlled_buffer_14
  Clock clock_1 (.out(C_CLOCK));
  POR por_1 (.out(por_1_out));
  Button RESET (.out(RESET_out));
  Multiplexer #(.width(8)) multiplexer_12 (
    .in0(controlled_buffer_9_out), .in1(8'hf0), .out(multiplexer_12_out), .sel(d_ff_1_q));
  Register CIR (.D(multiplexer_12_out), .en(or_3_out), .clk(C_CLOCK), .Q(CIR_q), .clr(C_RESET));
  or or_3 (or_3_out, d_ff_1_q, C_CIR_LATCH);
  Register #(.width(4)) MIC (.D(adder_2_out), .en(1'b1), .clk(C_CLOCK), .Q(MIC_q), .clr(d_ff_1_q));
  // Probe on C_CLOCK
  // Probe on C_PC_LATCH
  // Probe on C_PC_ENABLE
  // Probe on C_MAR_LATCH
  // Probe on C_MEM_WRITE
  // Probe on C_RESET
  // Probe on C_MEM_READ
  // Probe on C_MDR_ENABLE
  // Probe on C_MDR_LATCH
  // Probe on C_IDX_LATCH
  // Probe on C_IDX_ENABLE
  // Probe on C_CIR_LATCH
  // Probe on C_RA_LATCH
  // Probe on C_RA_ENABLE
  // Probe on C_RB_LATCH
  // Probe on C_RB_ENABLE
  // Probe on C_ALU_IDX_SEL
  // Probe on C_ALU_ADD_ENABLE
  // Probe on C_ALU_DATA_ENABLE
  // Probe on C_TX_L
  // Probe on C_TX_H
  // Probe on C_ALU_BW_OP
  // Probe on C_ALU_SFT_OP
  // Probe on undriven
  // Probe on undriven_2
  // Probe on undriven_3
  // Probe on undriven_4
  // Probe on CBUS_2[11]
  // Probe on CBUS_2[12]
  // Probe on CBUS_2[13]
  // Probe on CBUS_2[14]
  // Probe on CBUS_2[15]
  Pull_Resistor pull_resistor_5 (.node({CBUS_2, C_ALU_SFT_OP, C_ALU_BW_OP, C_TX_H, C_TX_L, C_ALU_DATA_ENABLE, C_ALU_ADD_ENABLE, C_ALU_IDX_SEL}));
  or or_4 (or_4_out, por_1_out, RESET_out);
  Adder #(.width(4)) adder_2 (.a(4'b0001), .b(MIC_q), .out(adder_2_out));  // open: cin, cout
  Pull_Resistor pull_resistor_6 (.node({C_RB_ENABLE, C_RB_LATCH, C_RA_ENABLE, C_RA_LATCH, C_CIR_LATCH, C_IDX_ENABLE, C_IDX_LATCH, C_MDR_LATCH, C_MDR_ENABLE, C_MEM_READ, C_RESET, C_MEM_WRITE, C_MAR_LATCH, C_PC_ENABLE, C_PC_LATCH, C_CLOCK}));
  D_Flip_Flop d_ff_1 (.D(or_4_out), .clk(C_CLOCK), .Q(d_ff_1_q));  // open: Qn, preset, reset
  ROM #(.dataWidth(16)) rom_2 (
    .addr({CIR_q[7:4], MIC_q}),
    .data({C_RB_ENABLE, C_RB_LATCH, C_RA_ENABLE, C_RA_LATCH, C_CIR_LATCH, C_IDX_ENABLE, C_IDX_LATCH, C_MDR_LATCH, C_MDR_ENABLE, C_MEM_READ, C_RESET, C_MEM_WRITE, C_MAR_LATCH, C_PC_ENABLE, C_PC_LATCH, C_CLOCK}));
  ROM #(.dataWidth(16)) rom_3 (
    .addr({CIR_q[7:4], MIC_q}),
    .data({CBUS_2, C_ALU_SFT_OP, C_ALU_BW_OP, C_TX_H, C_TX_L, C_ALU_DATA_ENABLE, C_ALU_ADD_ENABLE, C_ALU_IDX_SEL}));

  // Other names for the same wires on the sheet: CBUS_1[15:0] = {C_RB_ENABLE, C_RB_LATCH, C_RA_ENABLE, C_RA_LATCH, C_CIR_LATCH, C_IDX_ENABLE, C_IDX_LATCH, C_MDR_LATCH, C_MDR_ENABLE, C_MEM_READ, C_RESET, C_MEM_WRITE, C_MAR_LATCH, C_PC_ENABLE, C_PC_LATCH, C_CLOCK};
  //   CBUS_2[10:0] = {C_ALU_SFT_OP, C_ALU_BW_OP, C_TX_H, C_TX_L, C_ALU_DATA_ENABLE, C_ALU_ADD_ENABLE, C_ALU_IDX_SEL}
endmodule
